# Fritzing sketch Micro Servo (saved by Fritzing 0.9.6b)
breadboards: 1

parts:
  J1 = Basic Servo
  Componente1 = Arduino Uno (Rev3) - ICSP
  R1 = Rotary Potentiometer (Small) [maximum_resistance=100kΩ package=THT]

nets:
  GND: J1.gnd, Componente1.GND, R1.leg1
  VCC: J1.vcc, Componente1.5V, R1.leg2
  N1: J1.pulse, Componente1.D2
  N2: Componente1.A0, R1.wiper
